# Fritzing sketch Davinci_controller_2022 (saved by Fritzing 0.9.9b)
circuit board: 7.79915cm x 9.30092cm
breadboards: 2

parts:
  104 = Ceramic Capacitor [capacitance=0.1µF voltage=35V package="100 mil [THT, multilayer]"]
  33uF = Electrolytic Capacitor [capacitance=33µF voltage=10V package="100 mil [THT, electrolytic]"]
  PTC = Resettable Fuse PTC [package=ptc]
  Pch = Basic FET P-Channel [package="TO220 [THT]"]
  10K = Resistor [tolerance=±5% resistance=10k power=0.25 package=THT]
  D1 = Schottky Diode [part_number=1N5817 package="300 mil [THT]"]
  RESET = Pushbutton [package="[THT]"]
  10uF = Electrolytic Capacitor [capacitance=10µF voltage=10V package="100 mil [THT, electrolytic]"]
  10uF_2 = Electrolytic Capacitor [capacitance=10µF voltage=10V package="100 mil [THT, electrolytic]"]
  104_2 = Ceramic Capacitor [capacitance=100nF voltage=35V package="100 mil [THT, multilayer]"]
  104_3 = Ceramic Capacitor [capacitance=100nF voltage=35V package="100 mil [THT, multilayer]"]
  TB6612FNG = Motor Driver 1A Dual TB6612FNG [part_number=ROB_09457]
  A2 = JST XH 3A [form="♀ (female)" package=THT]
  A1 = JST XH 3A [form="♀ (female)" package=THT]
  A0 = JST XH 3A [form="♀ (female)" package=THT]
  A4 = JST XH 3A [form="♀ (female)" package=THT]
  A5 = JST XH 3A [form="♀ (female)" package=THT]
  A3 = JST XH 3A [form="♀ (female)" package=THT]
  A8 = JST XH 3A [form="♀ (female)" package=THT]
  A7 = JST XH 3A [form="♀ (female)" package=THT]
  A11 = JST XH 3A [form="♀ (female)" package=THT]
  A9 = JST XH 3A [form="♀ (female)" package=THT]
  A10 = JST XH 3A [form="♀ (female)" package=THT]
  MT1 = JST XH 2A [form="♀ (female)" package=THT]
  EXT = JST XH 2A [form="♀ (female)" package=THT]
  MT2 = JST XH 2A [form="♀ (female)" package=THT]
  BAT = JST XH 2A [form="♀ (female)" package=THT]
  I2C = JST XH 4A [form="♀ (female)" package=THT]
  I2C_2 = JST XH 4A [form="♀ (female)" package=THT]
  Davinci = IC, DIP package, 32 pins [chip_label=IC]
  A6 = JST XH 3A [form="♀ (female)" package=THT]
  START(D7) = Pushbutton [package="[THT]"]
  PWR_SW = Toggle Switch [package=THT]
  MT_SW = Toggle Switch [package=THT]
  Reg = Voltage Regulator - 5V [package="TO220 [THT]"]

nets:
  GND: 104.0, 33uF.-, RESET.Pin_3, RESET.Pin_4, 10uF.-, 10uF_2.-, 104_2.0, 104_3.0, TB6612FNG.GND, A2.pin3, A1.pin3, A0.pin3, A4.pin3, A5.pin3, A3.pin3, A8.pin3, A7.pin3, A11.pin3, A9.pin3, A10.pin3, EXT.pin2, BAT.pin2, I2C.pin4, I2C_2.pin4, Davinci.pin1, Davinci.pin16, Davinci.pin17, Davinci.pin32, A6.pin3, START(D7).Pin_1, START(D7).Pin_2, PWR_SW.COM, PWR_SW.L2, Reg.GND
  7.2V: 104.1, Pch.drain, 10uF_2.+, 104_2.1, TB6612FNG.VM, EXT.pin1, Reg.input_voltage
  N1: 33uF.+, D1.anode, Reg.output_voltage
  N2: PTC.1, BAT.pin1
  N3: PTC.2, Pch.source, 10K.Pin_0
  N4: Pch.gate, 10K.Pin_1, PWR_SW.L1
  5V: D1.cathode, 10uF.+, 104_3.1, TB6612FNG.VCC, A2.pin2, A1.pin2, A0.pin2, A4.pin2, A5.pin2, A3.pin2, A8.pin2, A7.pin2, A11.pin2, A9.pin2, A10.pin2, I2C.pin2, I2C_2.pin2, Davinci.pin2, A6.pin2, MT_SW.L1
  N5: RESET.Pin_1, RESET.Pin_2, Davinci.pin3
  PWMA: TB6612FNG.PWMA, Davinci.pin12
  AIN2: TB6612FNG.AIN2, Davinci.pin22
  AIN1: TB6612FNG.AIN1, Davinci.pin23
  STBY: TB6612FNG.STBY, MT_SW.COM
  BIN2: TB6612FNG.BIN1, Davinci.pin24
  BIN1: TB6612FNG.BIN2, Davinci.pin25
  PWMB: TB6612FNG.PWMB, Davinci.pin29
  N6: TB6612FNG.A01, MT1.pin2
  N7: TB6612FNG.A02, MT1.pin1
  N8: TB6612FNG.B02, MT2.pin2
  N9: TB6612FNG.B01, MT2.pin1
  A2: A2.pin1, Davinci.pin19
  A1: A1.pin1, Davinci.pin20
  A0: A0.pin1, Davinci.pin21
  A4: A4.pin1, Davinci.pin15
  A5: A5.pin1, Davinci.pin14
  A3: A3.pin1, Davinci.pin18
  A8: A8.pin1, Davinci.pin26
  A7: A7.pin1, Davinci.pin11
  A11: A11.pin1, Davinci.pin10
  A9: A9.pin1, Davinci.pin27
  A10: A10.pin1, Davinci.pin28
  SCL: I2C.pin1, I2C_2.pin1, Davinci.pin4
  SDA: I2C.pin3, I2C_2.pin3, Davinci.pin5
  A6: Davinci.pin8, A6.pin1
  N10: Davinci.pin30, START(D7).Pin_3, START(D7).Pin_4

notes:
  RX
  TX
  SIG 5V GND
  +  -
  D30
  D13
  ON
  GND 5V SIG
  SCL 5V SDA GND
  GND
  GND SDA 5V SCL
  RESET
  START(D7)
  EXT
  MT1
  MT2
  A1
  A3
  A5
  A7
  A9
  A11
  A0
  A2
  A4
  A10
  A6
  A8
  BAT
  Controller
  @ohguma
  2022-03
  IN GND OUT
  D5 (12)->PWMA
  D11(29)->PWMB
  D17(22)->INA2
  D15(23)->INA1
  D16(24)->INB1
  D14(25)->INB2
  6-16V
  D17
  D15
  D16
  D14
  D11
  D7
  AEF
  5V
  /RESET
  SCL
  SDA
  D5
  VM
  VCC
  A01
  A02
  B02
  B01
  BIN2
  PWMA
  BIN1
  STBY
  AIN1
  AIN2
  PWMB
  G  D  S
  PWR SW
  MT SW
  |
  Davinci

custom parts:
  Motor Driver 1A Dual TB6612FNG: The TB6612FNG motor driver can control up to two DC motors at a constant current of 1.2A (3.2A peak). Two input signals (IN1 and IN2) can be used to control the motor in one of four function modes - CW, CCW, short-brake, and stop. The two motor outputs (A and B) can be separately controlled, the speed of each motor is controlled via a PWM input signal with a frequency up to 100kHz. The STBY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
  JST XH 3A: JST XH-3A
  JST XH 2A: JST XH-2A
  JST XH 4A: JST XH-3A
